# Fritzing sketch Sketch (saved by Fritzing 0.9.3b)
breadboards: 1

parts:
  부품1 = Arduino Uno (Rev3)
  LED1 = 7-SEGMENT-4DIGIT-YOUNGSUN [package=7-segment-4digit-youngsun-longpads]
  R1 = Resistor [tolerance=±5% resistance=220 package=THT]
  R2 = Resistor [tolerance=±5% resistance=220 package=THT]
  R3 = Resistor [tolerance=±5% resistance=220 package=THT]
  R4 = Resistor [tolerance=±5% resistance=220 package=THT]
  hc-sr1 = hc-sr04
  부품2 = IR Receiver Breakout [package=PCB]

nets:
  N1: 부품1.A0, R4.Pin_1
  N2: 부품1.A1, hc-sr1.Trig
  N3: 부품1.A4/SDA, R2.Pin_1
  N4: 부품1.A5/SCL, R1.Pin_1
  N5: 부품1.D8, LED1.DIG2
  N6: 부품1.D9_PWM, LED1.C
  N7: 부품1.D10_PWM/SS, LED1.DIG3
  N8: 부품1.D11_PWM/MOSI, LED1.COL-A
  N9: 부품1.D12/MISO, R3.Pin_1
  N10: 부품1.D2, 부품2.OUT
  N11: 부품1.D3_PWM, hc-sr1.Echo
  N12: 부품1.D4, LED1.A
  N13: 부품1.D5_PWM, LED1.APOS-A
  N14: 부품1.D6_PWM, LED1.E
  N15: 부품1.D7, LED1.D
  VCC: 부품1.5V, hc-sr1.VCC, 부품2.VCC
  GND: 부품1.GND, hc-sr1.GND, 부품2.GND
  N16: LED1.DP, R4.Pin_0
  N17: LED1.F, R3.Pin_0
  N18: LED1.COL-C, R2.Pin_0
  N19: LED1.G, R1.Pin_0
